# Fritzing sketch tenzov2 (saved by Fritzing 0.9.3b)
breadboards: 1

parts:
  Part1 = Bluetooth Mate Silver  # not connected
  GY1 = MPU-6050 Board GY-521 [form="♀ (female)" package=THT]  # not connected
  GPS1 = Adafruit Ultimate GPS Breakout  # not connected
  JP1 = Header 6 [package=1x06-smd]
  Tiny_RTC1 = Tiny RTC

nets:
  N1: JP1.1, JP1.6
  N2: JP1.2, JP1.5
  N3: JP1.3, JP1.4
  N4: Tiny_RTC1.DS#0, Tiny_RTC1.SCL#1
  N5: Tiny_RTC1.SQ, Tiny_RTC1.DS#6, Tiny_RTC1.SCL#7
  N6: Tiny_RTC1.GND#10, Tiny_RTC1.BAT

custom parts:
  MPU-6050 Board GY-521: Acelerometro y Giroscopio MPU-6050 Board GY-521
  Tiny RTC: Tiny RTC I2C module DS1370Z RTC and AT24C32 EEPROM
